// Logisim project BFCPU.circ as structural Verilog: 14 circuits, main circuit main
module main (
  input  CLR,
  output CK,
  output RAM_CK,
  output WO_CLOCK,
  output out_5
);

  wire decoder_v3_1_p4, decoder_v3_1_p5, decoder_v3_1_p12, not_1_out, not_2_out, not_3_out, not_4_out;
  wire [1:0] decoder_v3_1_p6, decoder_v3_1_p10, decoder_v3_1_p16;
  wire [2:0] decoder_v3_1_p8, decoder_v3_1_p13;
  wire [7:0] address_counter_1_counter_out, alu_1_alu_out, general_register_1_r_out, main_memory_1_bath_out,
       rom_1_data;

  // Probe on main_memory_1_bath_out
  // Probe on alu_1_alu_out
  not not_1 (not_1_out, decoder_v3_1_p12);
  TTY tty_1 (.data(main_memory_1_bath_out[6:0]), .clk(CK), .we(decoder_v3_1_p12), .clr(CLR));
  ROM rom_1 (.addr(address_counter_1_counter_out), .data(rom_1_data));
  Clock clock_1 ();  // open: out
  general_register general_register_1 (
    .R_IN(main_memory_1_bath_out), .LD(not_1_out), .CK(CK), .CLR(not_2_out), .R_OUT(general_register_1_r_out));
  // Probe on general_register_1_r_out
  not not_2 (not_2_out, CLR);
  ALU alu_1 (
    .ALU_IN(main_memory_1_bath_out), .NOCHANGE_GATE(decoder_v3_1_p13[0]),
    .DECREMENT_GATE(decoder_v3_1_p13[1]), .INCREMENT_GATE(decoder_v3_1_p13[2]), .ALU_OUT(alu_1_alu_out));
  Clock clock_2 (.out(RAM_CK));
  not not_3 (not_3_out, RAM_CK);
  not not_4 (not_4_out, CLR);
  T_Flip_Flop t_ff_1 (.T(1'b1), .clk(RAM_CK), .Q(WO_CLOCK));  // open: Qn, reset, preset
  T_Flip_Flop t_ff_2 (.T(1'b1), .clk(not_3_out), .Qn(CK));  // open: Q, reset, preset
  // decoder_v3 decoder_v3_1: pin names not known; wires that end beside it: not_4_out, CK, rom_1_data, decoder_v3_1_p4, decoder_v3_1_p5, decoder_v3_1_p6[0], decoder_v3_1_p6[1], decoder_v3_1_p8[0], decoder_v3_1_p8[1], decoder_v3_1_p10[0], decoder_v3_1_p10[1], decoder_v3_1_p12, decoder_v3_1_p13[0], decoder_v3_1_p13[1], decoder_v3_1_p13[2], decoder_v3_1_p16[0], decoder_v3_1_p16[1], decoder_v3_1_p8[2], out_5
  main_memory main_memory_1 (
    .HALF_CK(RAM_CK), .SYS_CK(WO_CLOCK), .CK(CK), .CLR(not_4_out), .ADR_GATE(decoder_v3_1_p16[0]),
    .VAL_GATE(decoder_v3_1_p16[1]), .ADR_LD(decoder_v3_1_p6[0]), .RAM_LD(decoder_v3_1_p6[1]),
    .BATH_IN(alu_1_alu_out), .BATH_OUT(main_memory_1_bath_out), .COMPARE1_OUT(decoder_v3_1_p4));
  compStNp compstnp_1 (
    .CK(CK), .CLR(not_4_out), .STACKP_LD(decoder_v3_1_p8[0]), .NESTP_LD(decoder_v3_1_p8[1]),
    .STACKP_GATE(decoder_v3_1_p8[2]), .STNEP_IN(alu_1_alu_out), .STNEP_OUT(main_memory_1_bath_out),
    .COMPARE2_OUT(decoder_v3_1_p5));
  address_counter address_counter_1 (
    .HALF_CK(RAM_CK), .SYS_CK(WO_CLOCK), .STACK_ADR(alu_1_alu_out), .CK(WO_CLOCK), .CLR(not_4_out),
    .STACK_LD(decoder_v3_1_p10[0]), .COUNTER_LD(decoder_v3_1_p10[1]),
    .COUNTER_OUT(address_counter_1_counter_out));

  // Notes on the sheet:
  //   contents of rom_1 (hex, n*v repeats v):
  //   65*2 7 2 7 2 7 0 10*2 7 6*3 7 8*3 7 0 0 2 7 0 2 2 7
endmodule

module main_memory (
  input  HALF_CK,
  input  SYS_CK,
  input  CK,
  input  CLR,
  input  ADR_GATE,
  input  VAL_GATE,
  input  ADR_LD,
  input  RAM_LD,
  input  [7:0] BATH_IN,
  output [7:0] BATH_OUT,
  output COMPARE1_OUT
);

  wire n7432_1_pin3, not_1_out, not_2_out, not_3_out, not_4_out, not_5_out, not_6_out, not_7_out, not_8_out,
       not_9_out, not_10_out;
  wire [7:0] controlled_buffer_2_out, general_register_1_r_out, general_register_2_r_out, ram_1_data;

  not not_1 (not_1_out, HALF_CK);
  not not_2 (not_2_out, SYS_CK);
  assign BATH_OUT = not_3_out ? general_register_1_r_out : 8'bz;  // Controlled_Buffer controlled_buffer_1
  not not_3 (not_3_out, ADR_GATE);
  general_register general_register_1 (
    .R_IN(BATH_IN), .LD(ADR_LD), .CK(CK), .CLR(CLR), .R_OUT(general_register_1_r_out));
  _7432 #(.ShowInternalStructure("true")) u_7432_1 (
    .pin1(SYS_CK), .pin2(RAM_LD), .pin3(n7432_1_pin3));  // open: pin4, pin5, pin6, pin13, pin12, pin11, pin10, pin9, pin8
  not not_4 (not_4_out, CLR);
  RAM #(.clearpin("true"), .databus("bidir")) ram_1 (
    .addr(general_register_1_r_out), .we(not_5_out), .oe(not_6_out), .clk(not_1_out), .data(ram_1_data),
    .clr(not_4_out));
  not not_5 (not_5_out, n7432_1_pin3);
  not not_6 (not_6_out, not_2_out);
  not not_7 (not_7_out, SYS_CK);
  assign controlled_buffer_2_out = not_8_out ? ram_1_data : 8'bz;  // Controlled_Buffer controlled_buffer_2
  not not_8 (not_8_out, not_2_out);
  assign ram_1_data = not_9_out ? BATH_IN : 8'bz;  // Controlled_Buffer controlled_buffer_3
  not not_9 (not_9_out, SYS_CK);
  not not_10 (not_10_out, VAL_GATE);
  general_register general_register_2 (
    .R_IN(controlled_buffer_2_out), .LD(not_7_out), .CK(HALF_CK), .CLR(CLR), .R_OUT(general_register_2_r_out));
  assign BATH_OUT = not_10_out ? general_register_2_r_out : 8'bz;  // Controlled_Buffer controlled_buffer_4
  compare1 compare1_1 (.COMPARE2_IN(general_register_2_r_out), .COMPARE1_OUT(COMPARE1_OUT));
endmodule

module general_register (
  input  [7:0] R_IN,
  input  LD,
  input  CK,
  input  CLR,
  output [7:0] R_OUT
);

  wire n74161_1_pin7;

  _74161 #(.ShowInternalStructure("true")) u_74161_1 (
    .pin1(CLR), .pin2(CK), .pin3(R_IN[0]), .pin4(R_IN[1]), .pin5(R_IN[2]), .pin6(R_IN[3]),
    .pin7(n74161_1_pin7), .pin14(R_OUT[0]), .pin13(R_OUT[1]), .pin12(R_OUT[2]), .pin11(R_OUT[3]),
    .pin10(n74161_1_pin7), .pin9(LD));  // open: pin15
  _74161 #(.ShowInternalStructure("true")) u_74161_2 (
    .pin1(CLR), .pin2(CK), .pin3(R_IN[4]), .pin4(R_IN[5]), .pin5(R_IN[6]), .pin6(R_IN[7]),
    .pin7(n74161_1_pin7), .pin14(R_OUT[4]), .pin13(R_OUT[5]), .pin12(R_OUT[6]), .pin11(R_OUT[7]),
    .pin10(n74161_1_pin7), .pin9(LD));  // open: pin15
  // also tied to GND on the sheet: n74161_1_pin7
endmodule

module compare2 (
  input  [7:0] COMPARE2_IN,
  input  [7:0] COMPARE2_MINUS_IN,
  output COMPARE2_OUT
);

  wire n7402_1_pin1, n7402_1_pin2, n7402_1_pin3, n7402_1_pin4, n7402_1_pin5, n7402_1_pin6, n7402_1_pin10,
       n7402_1_pin13, n7404_1_pin2, n7404_1_pin4, n7404_1_pin10, n7404_1_pin12, n7404_2_pin2, n7404_2_pin4,
       n7404_2_pin10, n7404_2_pin12, n7408_1_pin3, n7408_1_pin5, n74283_1_pin1, n74283_1_pin4, n74283_1_pin7,
       n74283_1_pin9, n74283_1_pin10, n74283_1_pin13;

  _7404 #(.ShowInternalStructure("true")) u_7404_1 (
    .pin1(COMPARE2_IN[0]), .pin2(n7404_1_pin2), .pin3(COMPARE2_IN[1]), .pin4(n7404_1_pin4),
    .pin13(COMPARE2_IN[2]), .pin12(n7404_1_pin12), .pin11(COMPARE2_IN[3]), .pin10(n7404_1_pin10));  // open: pin5, pin6, pin9, pin8
  _74283 #(.ShowInternalStructure("true")) u_74283_1 (
    .pin1(n74283_1_pin1), .pin2(n7404_1_pin4), .pin3(COMPARE2_MINUS_IN[1]), .pin4(n74283_1_pin4),
    .pin5(COMPARE2_MINUS_IN[0]), .pin6(n7404_1_pin2), .pin7(n74283_1_pin7), .pin15(n7404_1_pin12),
    .pin14(COMPARE2_MINUS_IN[2]), .pin13(n74283_1_pin13), .pin12(COMPARE2_MINUS_IN[3]),
    .pin11(n7404_1_pin10), .pin10(n74283_1_pin10), .pin9(n74283_1_pin9));
  _7402 #(.ShowInternalStructure("true")) u_7402_1 (
    .pin1(n7402_1_pin1), .pin2(n7402_1_pin2), .pin3(n7402_1_pin3), .pin4(n7402_1_pin4), .pin5(n7402_1_pin5),
    .pin6(n7402_1_pin6), .pin13(n7402_1_pin13), .pin12(n74283_1_pin4), .pin11(n74283_1_pin1),
    .pin10(n7402_1_pin10), .pin9(n74283_1_pin13), .pin8(n74283_1_pin10));
  _7408 #(.ShowInternalStructure("true")) u_7408_1 (
    .pin1(n7402_1_pin10), .pin2(n7402_1_pin13), .pin3(n7408_1_pin3), .pin4(n7408_1_pin3),
    .pin5(n7408_1_pin5), .pin6(COMPARE2_OUT), .pin13(n7402_1_pin4), .pin12(n7402_1_pin1), .pin11(n7408_1_pin5));  // open: pin10, pin9, pin8
  _7404 #(.ShowInternalStructure("true")) u_7404_2 (
    .pin1(COMPARE2_IN[4]), .pin2(n7404_2_pin2), .pin3(COMPARE2_IN[5]), .pin4(n7404_2_pin4),
    .pin13(COMPARE2_IN[6]), .pin12(n7404_2_pin12), .pin11(COMPARE2_IN[7]), .pin10(n7404_2_pin10));  // open: pin5, pin6, pin9, pin8
  _74283 #(.ShowInternalStructure("true")) u_74283_2 (
    .pin1(n7402_1_pin5), .pin2(n7404_2_pin4), .pin3(COMPARE2_MINUS_IN[5]), .pin4(n7402_1_pin6),
    .pin5(COMPARE2_MINUS_IN[4]), .pin6(n7404_2_pin2), .pin7(n74283_1_pin9), .pin15(n7404_2_pin12),
    .pin14(COMPARE2_MINUS_IN[6]), .pin13(n7402_1_pin3), .pin12(COMPARE2_MINUS_IN[7]), .pin11(n7404_2_pin10),
    .pin10(n7402_1_pin2));  // open: pin9
  // also tied to GND on the sheet: n74283_1_pin7
endmodule

module compare1 (
  input  [7:0] COMPARE2_IN,
  output COMPARE1_OUT
);

  wire n7432_1_pin3, n7432_1_pin5, n7432_1_pin9, n7432_2_pin3, n7432_2_pin11;

  _7432 #(.ShowInternalStructure("true")) u_7432_1 (
    .pin1(COMPARE2_IN[6]), .pin2(COMPARE2_IN[7]), .pin3(n7432_1_pin3), .pin4(n7432_1_pin3),
    .pin5(n7432_1_pin5), .pin13(COMPARE2_IN[5]), .pin12(COMPARE2_IN[4]), .pin11(n7432_1_pin5),
    .pin10(n7432_1_pin5), .pin9(n7432_1_pin9), .pin8(COMPARE1_OUT));  // open: pin6
  _7432 #(.ShowInternalStructure("true")) u_7432_2 (
    .pin1(COMPARE2_IN[2]), .pin2(COMPARE2_IN[3]), .pin3(n7432_2_pin3), .pin13(COMPARE2_IN[1]),
    .pin12(COMPARE2_IN[0]), .pin11(n7432_2_pin11), .pin10(n7432_2_pin11), .pin9(n7432_2_pin3),
    .pin8(n7432_1_pin9));  // open: pin4, pin5, pin6
endmodule

module stack_memory (
  input  HALF_CK,
  input  SYS_CK,
  input  [7:0] STACK_ADR,
  input  CLR,
  input  STACK_LD,
  input  [7:0] STACK_IN,
  output [7:0] STACK_OUT
);

  wire n7432_1_pin3, n74283_1_pin3, n74283_1_pin5, n74283_1_pin7, n74283_1_pin9, n74283_1_pin12,
       n74283_1_pin14, n74283_2_pin3, n74283_2_pin5, n74283_2_pin12, n74283_2_pin14, not_1_out, not_2_out,
       not_3_out, not_4_out, not_5_out, not_6_out, not_7_out, not_8_out;
  wire [7:0] controlled_buffer_1_out, n74283_1_pin4, ram_1_data;

  not not_1 (not_1_out, HALF_CK);
  not not_2 (not_2_out, SYS_CK);
  _74283 #(.ShowInternalStructure("true")) u_74283_1 (
    .pin1(n74283_1_pin4[1]), .pin2(STACK_IN[1]), .pin3(n74283_1_pin3), .pin4(n74283_1_pin4[0]),
    .pin5(n74283_1_pin5), .pin6(STACK_IN[0]), .pin7(n74283_1_pin7), .pin15(STACK_IN[2]),
    .pin14(n74283_1_pin14), .pin13(n74283_1_pin4[2]), .pin12(n74283_1_pin12), .pin11(STACK_IN[3]),
    .pin10(n74283_1_pin4[3]), .pin9(n74283_1_pin9));
  RAM #(.clearpin("true"), .databus("bidir")) ram_1 (
    .addr(STACK_ADR), .we(not_3_out), .oe(not_4_out), .clk(not_1_out), .data(ram_1_data));  // open: clr
  not not_3 (not_3_out, n7432_1_pin3);
  not not_4 (not_4_out, not_2_out);
  _7432 #(.ShowInternalStructure("true")) u_7432_1 (
    .pin1(SYS_CK), .pin2(STACK_LD), .pin3(n7432_1_pin3));  // open: pin4, pin5, pin6, pin13, pin12, pin11, pin10, pin9, pin8
  _74283 #(.ShowInternalStructure("true")) u_74283_2 (
    .pin1(n74283_1_pin4[5]), .pin2(STACK_IN[5]), .pin3(n74283_2_pin3), .pin4(n74283_1_pin4[4]),
    .pin5(n74283_2_pin5), .pin6(STACK_IN[4]), .pin7(n74283_1_pin9), .pin15(STACK_IN[6]),
    .pin14(n74283_2_pin14), .pin13(n74283_1_pin4[6]), .pin12(n74283_2_pin12), .pin11(STACK_IN[7]),
    .pin10(n74283_1_pin4[7]));  // open: pin9
  not not_5 (not_5_out, SYS_CK);
  not not_6 (not_6_out, CLR);
  assign controlled_buffer_1_out = not_7_out ? ram_1_data : 8'bz;  // Controlled_Buffer controlled_buffer_1
  not not_7 (not_7_out, not_2_out);
  assign ram_1_data = not_8_out ? n74283_1_pin4 : 8'bz;  // Controlled_Buffer controlled_buffer_2
  not not_8 (not_8_out, SYS_CK);
  general_register general_register_1 (
    .R_IN(controlled_buffer_1_out), .LD(not_5_out), .CK(HALF_CK), .CLR(CLR), .R_OUT(STACK_OUT));
  // also tied to GND on the sheet: {n74283_1_pin3, n74283_1_pin5, n74283_1_pin14, n74283_1_pin12, n74283_2_pin3, n74283_2_pin5, n74283_2_pin14, n74283_2_pin12}
  // also tied to VCC on the sheet: n74283_1_pin7
endmodule

module address_counter (
  input  HALF_CK,
  input  SYS_CK,
  input  [7:0] STACK_ADR,
  input  CK,
  input  CLR,
  input  STACK_LD,
  input  COUNTER_LD,
  output [7:0] COUNTER_OUT
);

  wire n74161_1_pin7, n74161_1_pin15;
  wire [7:0] n74161_1_pin3;

  _74161 u_74161_1 (
    .pin1(CLR), .pin2(CK), .pin3(n74161_1_pin3[0]), .pin4(n74161_1_pin3[1]), .pin5(n74161_1_pin3[2]),
    .pin6(n74161_1_pin3[3]), .pin7(n74161_1_pin7), .pin15(n74161_1_pin15), .pin14(COUNTER_OUT[0]),
    .pin13(COUNTER_OUT[1]), .pin12(COUNTER_OUT[2]), .pin11(COUNTER_OUT[3]), .pin10(n74161_1_pin7),
    .pin9(COUNTER_LD));
  _74161 #(.ShowInternalStructure("true")) u_74161_2 (
    .pin1(CLR), .pin2(CK), .pin3(n74161_1_pin3[4]), .pin4(n74161_1_pin3[5]), .pin5(n74161_1_pin3[6]),
    .pin6(n74161_1_pin3[7]), .pin7(n74161_1_pin15), .pin14(COUNTER_OUT[4]), .pin13(COUNTER_OUT[5]),
    .pin12(COUNTER_OUT[6]), .pin11(COUNTER_OUT[7]), .pin10(n74161_1_pin7), .pin9(COUNTER_LD));  // open: pin15
  stack_memory stack_memory_1 (
    .HALF_CK(HALF_CK), .SYS_CK(SYS_CK), .STACK_ADR(STACK_ADR), .CLR(CLR), .STACK_LD(STACK_LD),
    .STACK_IN(COUNTER_OUT), .STACK_OUT(n74161_1_pin3));
  // also tied to VCC on the sheet: n74161_1_pin7
endmodule

module compStNp (
  input  CK,
  input  CLR,
  input  STACKP_LD,
  input  NESTP_LD,
  input  STACKP_GATE,
  input  [7:0] STNEP_IN,
  output [7:0] STNEP_OUT,
  output COMPARE2_OUT
);

  wire not_1_out, not_2_out, not_3_out;
  wire [7:0] general_register_1_r_out, general_register_2_r_out;

  not not_1 (not_1_out, STACKP_LD);
  not not_2 (not_2_out, NESTP_LD);
  general_register general_register_1 (
    .R_IN(STNEP_IN), .LD(not_1_out), .CK(CK), .CLR(CLR), .R_OUT(general_register_1_r_out));
  assign STNEP_OUT = not_3_out ? general_register_1_r_out : 8'bz;  // Controlled_Buffer controlled_buffer_1
  not not_3 (not_3_out, STACKP_GATE);
  // Probe on general_register_2_r_out
  general_register general_register_2 (
    .R_IN(general_register_1_r_out), .LD(not_2_out), .CK(CK), .CLR(CLR), .R_OUT(general_register_2_r_out));
  compare2 compare2_1 (
    .COMPARE2_IN(general_register_2_r_out), .COMPARE2_MINUS_IN(general_register_1_r_out),
    .COMPARE2_OUT(COMPARE2_OUT));
endmodule

module Dff8bit (
  input  CLR,
  input  CK,
  input  [7:0] DFF_IN,
  output [7:0] out_4
);

  _74273 #(.ShowInternalStructure("true")) u_74273_1 (
    .pin1(CLR), .pin2(out_4[0]), .pin3(DFF_IN[0]), .pin4(DFF_IN[1]), .pin5(out_4[1]), .pin6(out_4[2]),
    .pin7(DFF_IN[2]), .pin8(DFF_IN[3]), .pin9(out_4[3]), .pin19(out_4[7]), .pin18(DFF_IN[7]),
    .pin17(DFF_IN[6]), .pin16(out_4[6]), .pin15(out_4[5]), .pin14(DFF_IN[5]), .pin13(DFF_IN[4]),
    .pin12(out_4[4]), .pin11(CK));
endmodule

module ALU (
  input  [7:0] ALU_IN,
  input  NOCHANGE_GATE,
  input  DECREMENT_GATE,
  input  INCREMENT_GATE,
  output [7:0] ALU_OUT
);

  wire and_1_out, n74283_1_pin9, not_1_out, not_2_out, not_3_out;
  wire [7:0] n74283_1_pin4;

  not not_1 (not_1_out, DECREMENT_GATE);
  not not_2 (not_2_out, INCREMENT_GATE);
  and and_1 (and_1_out, NOCHANGE_GATE, DECREMENT_GATE, INCREMENT_GATE);
  not not_3 (not_3_out, and_1_out);
  assign ALU_OUT = not_3_out ? n74283_1_pin4 : 8'bz;  // Controlled_Buffer controlled_buffer_1
  _74283 #(.ShowInternalStructure("true")) u_74283_1 (
    .pin1(n74283_1_pin4[1]), .pin2(not_1_out), .pin3(ALU_IN[1]), .pin4(n74283_1_pin4[0]), .pin5(ALU_IN[0]),
    .pin6(not_1_out), .pin7(not_2_out), .pin15(not_1_out), .pin14(ALU_IN[2]), .pin13(n74283_1_pin4[2]),
    .pin12(ALU_IN[3]), .pin11(not_1_out), .pin10(n74283_1_pin4[3]), .pin9(n74283_1_pin9));
  _74283 #(.ShowInternalStructure("true")) u_74283_2 (
    .pin1(n74283_1_pin4[5]), .pin2(not_1_out), .pin3(ALU_IN[5]), .pin4(n74283_1_pin4[4]), .pin5(ALU_IN[4]),
    .pin6(not_1_out), .pin7(n74283_1_pin9), .pin15(not_1_out), .pin14(ALU_IN[6]), .pin13(n74283_1_pin4[6]),
    .pin12(ALU_IN[7]), .pin11(not_1_out), .pin10(n74283_1_pin4[7]));  // open: pin9
endmodule

module decoder_bf (
  input  CLR,
  input  CK,
  input  [7:0] INSTRUCTION,
  input  detect_0,
  input  detect_equal,
  output reg_out,
  output reg_sp,
  output reg_np,
  output RAM_KeepStack,
  output RAM_VALUE,
  output REG_ADRS,
  output PC,
  output INPUT_GATE,
  output NOCHANGE_GATE,
  output DECREMENT_GATE,
  output INCREMENT_GATE,
  output ADR_GATE,
  output VAL_GATE,
  output STACKP_GATE,
  output FLAG_OUT
);

  wire and_4_out, and_5_out, and_7_out, and_8_out, and_9_out, not_2_out, not_3_out, not_4_out, not_5_out,
       not_6_out, or_1_out, or_3_out, or_4_out, or_5_out, or_7_out, or_10_out, or_11_out;

  or or_1 (or_1_out, FLAG_OUT, INSTRUCTION[2], INSTRUCTION[1]);
  or or_2 (REG_ADRS, or_1_out, INSTRUCTION[3]);
  or or_3 (or_3_out, INSTRUCTION[2], not_3_out);
  and and_1 (RAM_VALUE, or_3_out, or_4_out);
  or or_4 (or_4_out, not_4_out, not_3_out, INSTRUCTION[0]);
  and and_2 (reg_sp, INSTRUCTION[2], not_3_out);
  and and_3 (reg_np, not_6_out, not_5_out, INSTRUCTION[2], not_3_out, not_2_out);
  or or_5 (or_5_out, reg_np, and_4_out);
  and and_4 (and_4_out, FLAG_OUT, detect_equal, INSTRUCTION[2], not_3_out, INSTRUCTION[0]);
  flag flag_1 (.CLR(CLR), .CK(CK), .FLAG_LD(or_5_out), .FLAG_OUT(FLAG_OUT));
  nand nand_1 (RAM_KeepStack, INSTRUCTION[2], not_3_out, not_2_out);
  not not_1 (PC, and_5_out);
  and and_5 (and_5_out, not_6_out, detect_0, INSTRUCTION[2], not_3_out, INSTRUCTION[0]);
  and and_6 (reg_out, INSTRUCTION[2], INSTRUCTION[1], INSTRUCTION[0]);
  nand nand_2 (INPUT_GATE, INSTRUCTION[2], INSTRUCTION[1], not_2_out);
  nand nand_3 (NOCHANGE_GATE, detect_0, INSTRUCTION[2], not_3_out, INSTRUCTION[0]);
  or or_6 (DECREMENT_GATE, and_7_out, and_8_out);
  and and_7 (and_7_out, detect_0, INSTRUCTION[2], not_3_out, INSTRUCTION[0]);
  and and_8 (and_8_out, not_2_out, or_7_out);
  or or_7 (or_7_out, not_3_out, not_4_out);
  or or_8 (INCREMENT_GATE, INSTRUCTION[0], and_9_out);
  and and_9 (and_9_out, INSTRUCTION[2], INSTRUCTION[1]);
  or or_9 (ADR_GATE, INSTRUCTION[1], INSTRUCTION[2]);
  and and_10 (VAL_GATE, or_10_out, or_11_out);
  or or_10 (or_10_out, INSTRUCTION[2], not_3_out);
  or or_11 (or_11_out, not_4_out, not_3_out, not_2_out);
  or or_12 (STACKP_GATE, INSTRUCTION[1], not_4_out);
  not not_2 (not_2_out, INSTRUCTION[0]);
  not not_3 (not_3_out, INSTRUCTION[1]);
  not not_4 (not_4_out, INSTRUCTION[2]);
  not not_5 (not_5_out, detect_0);
  not not_6 (not_6_out, FLAG_OUT);

  // Notes on the sheet:
  //   I(0)
  //   I(1)
  //   I(2)
  //   COMPARE1
  //   COMPARE2
  //   FLAG
  //   RAM val
  //   Reg SP
  //   Reg NP
  //   Reg Flag
  //   RAM keepStack
  //   command counter
  //   Output
  //   input Gate
  //   Buffer Gate
  //   -- Gate
  //   ++ Gate
  //   Address Gate 1
  //   Value Gate 1
  //   Stack Pointer Gate 1
  //   I(0)
  //   I(1)
  //   I(2)
endmodule

module flag (
  input  CLR,
  input  CK,
  input  FLAG_LD,
  output FLAG_OUT
);

  wire n74161_1_pin3, n74161_1_pin7, n74161_1_pin9, n74161_1_pin10;

  _74161 #(.ShowInternalStructure("true")) u_74161_1 (
    .pin1(CLR), .pin2(CK), .pin3(n74161_1_pin3), .pin7(n74161_1_pin7), .pin14(FLAG_OUT),
    .pin10(n74161_1_pin10), .pin9(n74161_1_pin9));  // open: pin4, pin5, pin6, pin15, pin13, pin12, pin11
  not not_1 (n74161_1_pin3, FLAG_OUT);
  not not_2 (n74161_1_pin9, FLAG_LD);
  // also tied to GND on the sheet: {n74161_1_pin10, n74161_1_pin7}
endmodule

module decoder_v3 (
  input  CLR,
  input  CK,
  input  FLAG_DEBUG,
  input  [7:0] INSTRUCTION,
  input  COMPARE1,
  input  COMAPRE2,
  output ADR_LD,
  output RAM_LD,
  output OUTPUT_LD,
  output FLAG_DEBUG_OUT,
  output STACKP_LD,
  output NESTP_LD,
  output DECREMENT_GATE,
  output STACK_LD,
  output COUNTER_LD,
  output INPUT_GATE,
  output NOCHANGE_GATE,
  output INCREMENT_GATE,
  output ADR_GATE,
  output VAL_GATE,
  output STACKP_GATE,
  output FLAG_OUT
);

  wire and_2_out, and_3_out, and_4_out, and_6_out, and_8_out, and_9_out, nand_3_out, nor_1_out, nor_2_out,
       not_1_out, not_2_out, not_3_out, not_4_out, not_6_out, not_8_out, not_9_out, not_10_out, or_6_out,
       or_7_out, or_8_out, or_10_out;

  or or_1 (INPUT_GATE, INSTRUCTION[0], not_1_out);
  not not_1 (not_1_out, and_3_out);
  and and_1 (OUTPUT_LD, and_2_out, not_2_out);
  not not_2 (not_2_out, FLAG_DEBUG);
  and and_2 (and_2_out, INSTRUCTION[0], and_3_out);
  and and_3 (and_3_out, INSTRUCTION[2], INSTRUCTION[1]);
  or or_2 (ADR_LD, INSTRUCTION[3], FLAG_DEBUG, ADR_GATE);
  or or_3 (ADR_GATE, INSTRUCTION[2], INSTRUCTION[1]);
  and and_4 (and_4_out, FLAG_DEBUG, COMAPRE2, INSTRUCTION[0], not_3_out);
  or or_4 (FLAG_DEBUG_OUT, and_4_out, NESTP_LD);
  not not_3 (not_3_out, STACKP_GATE);
  flag flag_1 (.CLR(CLR), .CK(CK), .FLAG_LD(FLAG_DEBUG_OUT));  // open: FLAG_OUT
  and and_5 (NESTP_LD, nor_1_out, nor_2_out);
  nor nor_1 (nor_1_out, COMPARE1, INSTRUCTION[0]);
  nand nand_1 (COUNTER_LD, COMPARE1, INSTRUCTION[0], nor_2_out);
  nor nor_2 (nor_2_out, FLAG_DEBUG, STACKP_GATE);
  or or_5 (RAM_LD, and_6_out, FLAG_DEBUG);
  and and_6 (and_6_out, or_6_out, or_7_out);
  or or_6 (or_6_out, INSTRUCTION[0], nand_3_out);
  and and_7 (VAL_GATE, or_7_out, or_8_out);
  or or_7 (or_7_out, INSTRUCTION[2], not_9_out);
  or or_8 (or_8_out, not_8_out, nand_3_out);
  nand nand_2 (INCREMENT_GATE, not_8_out, nand_3_out);
  nand nand_3 (nand_3_out, INSTRUCTION[2], INSTRUCTION[1]);
  or or_9 (DECREMENT_GATE, and_8_out, and_9_out);
  and and_8 (and_8_out, or_10_out, not_8_out);
  or or_10 (or_10_out, not_4_out, nand_3_out);
  not not_4 (not_4_out, nand_3_out);
  not not_5 (NOCHANGE_GATE, and_9_out);
  and and_9 (and_9_out, INSTRUCTION[0], COMPARE1, not_6_out);
  not not_6 (not_6_out, STACKP_GATE);
  or or_11 (STACK_LD, INSTRUCTION[0], STACKP_GATE);
  not not_7 (STACKP_LD, STACKP_GATE);
  nand nand_4 (STACKP_GATE, not_9_out, INSTRUCTION[2]);
  not not_8 (not_8_out, INSTRUCTION[0]);
  not not_9 (not_9_out, INSTRUCTION[1]);
  not not_10 (not_10_out, FLAG_DEBUG);

  assign FLAG_OUT = FLAG_DEBUG;

  // Notes on the sheet:
  //   I(0)
  //   I(1)
  //   I(2)
  //   COMPARE1
  //   COMPARE2
  //   FLAG
  //   alpha
  //   input Gate
  //   Output
  //   lambda
  //   Address Gate 1
  //   Reg Flag
  //   zeta
  //   Reg NP
  //   epsilon
  //   delta
  //   command counter
  //   RAM val
  //   beta
  //   ++ Gate
  //   gamma
  //   -- Gate
  //   Buffer Gate
  //   theta
  //   Value Gate 1
  //   RAM keepStack
  //   Reg SP
  //   Stack Pointer Gate 1
  //   alpha
  //   I(0)
  //   I(1)
  //   I(2)
endmodule

module decoder_remake2025 (
  input  CLR,
  input  CK,
  input  [7:0] INSTRUCTION,
  input  detect_0,
  input  detect_equal,
  output reg_out,
  output reg_sp,
  output reg_np,
  output RAM_KeepStack,
  output RAM_VALUE,
  output REG_ADRS,
  output PC,
  output INPUT_GATE,
  output NOCHANGE_GATE,
  output DECREMENT_GATE,
  output INCREMENT_GATE,
  output ADR_GATE,
  output VAL_GATE,
  output STACKP_GATE,
  output FLAG_OUT
);

  wire and_2_out, and_3_out, and_4_out, and_5_out, and_6_out, and_7_out, and_8_out, and_9_out, not_3_out,
       not_6_out, not_7_out, not_8_out, not_9_out, not_10_out, or_2_out, or_3_out, or_4_out, or_5_out,
       or_7_out, or_10_out, or_11_out;

  or or_1 (REG_ADRS, or_2_out, INSTRUCTION[3]);
  or or_2 (or_2_out, FLAG_OUT, INSTRUCTION[2], INSTRUCTION[1]);
  and and_1 (RAM_VALUE, or_3_out, or_4_out);
  or or_3 (or_3_out, INSTRUCTION[2], not_7_out);
  or or_4 (or_4_out, not_8_out, not_7_out, INSTRUCTION[0]);
  not not_1 (reg_sp, and_2_out);
  and and_2 (and_2_out, INSTRUCTION[2], not_7_out);
  not not_2 (reg_np, and_3_out);
  and and_3 (and_3_out, not_10_out, not_9_out, INSTRUCTION[2], not_7_out, not_6_out);
  not not_3 (not_3_out, or_5_out);
  or or_5 (or_5_out, and_3_out, and_4_out);
  and and_4 (and_4_out, FLAG_OUT, detect_equal, INSTRUCTION[2], not_7_out, INSTRUCTION[0]);
  flag flag_1 (.CLR(CLR), .CK(CK), .FLAG_LD(not_3_out), .FLAG_OUT(FLAG_OUT));
  nand nand_1 (RAM_KeepStack, INSTRUCTION[2], not_7_out, not_6_out);
  not not_4 (PC, and_5_out);
  and and_5 (and_5_out, not_10_out, detect_0, INSTRUCTION[2], not_7_out, INSTRUCTION[0]);
  not not_5 (reg_out, and_6_out);
  and and_6 (and_6_out, INSTRUCTION[2], INSTRUCTION[1], INSTRUCTION[0]);
  nand nand_2 (INPUT_GATE, INSTRUCTION[2], INSTRUCTION[1], not_6_out);
  nand nand_3 (NOCHANGE_GATE, detect_0, INSTRUCTION[2], not_7_out, INSTRUCTION[0]);
  and and_7 (and_7_out, detect_0, INSTRUCTION[2], not_7_out, INSTRUCTION[0]);
  or or_6 (DECREMENT_GATE, and_7_out, and_8_out);
  and and_8 (and_8_out, not_6_out, or_7_out);
  or or_7 (or_7_out, not_7_out, not_8_out);
  or or_8 (INCREMENT_GATE, INSTRUCTION[0], and_9_out);
  and and_9 (and_9_out, INSTRUCTION[2], INSTRUCTION[1]);
  or or_9 (ADR_GATE, INSTRUCTION[1], INSTRUCTION[2]);
  and and_10 (VAL_GATE, or_10_out, or_11_out);
  or or_10 (or_10_out, INSTRUCTION[2], not_7_out);
  or or_11 (or_11_out, not_8_out, not_7_out, not_6_out);
  or or_12 (STACKP_GATE, INSTRUCTION[1], not_8_out);
  not not_6 (not_6_out, INSTRUCTION[0]);
  not not_7 (not_7_out, INSTRUCTION[1]);
  not not_8 (not_8_out, INSTRUCTION[2]);
  not not_9 (not_9_out, detect_0);
  not not_10 (not_10_out, FLAG_OUT);

  // Notes on the sheet:
  //   COMPARE1
  //   COMPARE2
  //   FLAG
  //   I(0)
  //   I(1)
  //   I(2)
  //   RAM val
  //   Reg SP
  //   Reg NP
  //   Reg Flag
  //   RAM keepStack
  //   command counter
  //   Output
  //   input Gate
  //   Buffer Gate
  //   -- Gate
  //   ++ Gate
  //   Address Gate 1
  //   Value Gate 1
  //   Stack Pointer Gate 1
  //   I(0)
  //   I(1)
  //   I(2)
endmodule
