// Logisim project BF_Logi.circ as structural Verilog: 1 circuit, main circuit main
module main (
  input  [7:0] in_1,
  input  in_2,
  input  in_3,
  input  [1:0] in_4,
  input  [7:0] in_5,
  input  [7:0] in_6,
  input  [7:0] in_7,
  input  [1:0] in_8,
  input  in_9,
  input  in_10,
  input  in_11,
  input  [7:0] in_12,
  input  [1:0] ALU_Oup_Select,
  input  ALU_Inp_Select,
  output [7:0] out_15,
  output [7:0] out_16,
  output [7:0] out_17,
  output [7:0] out_18,
  output [7:0] out_19,
  output [7:0] out_20,
  output [7:0] out_21,
  output [7:0] out_22
);

  wire ck_out, clock_1_out, clock_2_out, not_1_out;
  wire [7:0] adder_3_out, counter_1_q, demultiplexer_1_out0, demultiplexer_1_out1, multiplexer_2_out,
       ram_1_dout, ram_2_dout, register_2_q, subtractor_3_out;

  Register register_1 ();  // open: D, en, clk, Q, clr
  Counter counter_1 (
    .clr(in_9), .load(in_10), .up(in_11), .clk(clock_1_out), .D(in_12), .Q(counter_1_q));  // open: count, carry
  Clock clock_1 (.out(clock_1_out));
  Adder adder_1 (.a(in_5), .b(in_6), .out(out_19));  // open: cin, cout
  Subtractor subtractor_1 (.a(in_5), .b(in_6), .out(out_20));  // open: bin, bout
  ROM rom_1 (.addr(counter_1_q), .data(out_21));
  Multiplexer #(.select(2), .width(8)) multiplexer_1 (
    .in0(in_5), .in1(out_19), .in2(out_20), .out(out_18), .sel(in_8));  // open: in3
  RAM ram_1 (.addr(in_1), .we(in_2), .oe(in_3), .clk(clock_2_out), .din(out_15), .dout(ram_1_dout));
  Clock clock_2 (.out(clock_2_out));
  Register register_2 (.D(demultiplexer_1_out0), .en(not_1_out), .clk(ck_out), .Q(register_2_q));  // open: clr
  Clock ck (.out(ck_out));
  not not_1 (not_1_out, ALU_Inp_Select);
  RAM ram_2 (
    .addr(register_2_q), .we(ALU_Inp_Select), .oe(1'b1), .clk(ck_out), .din(demultiplexer_1_out1),
    .dout(ram_2_dout));
  Adder adder_2 (.a(ram_1_dout), .b(in_7), .out(out_16));  // open: cin, cout
  Subtractor subtractor_2 (.a(ram_1_dout), .b(in_7), .out(out_17));  // open: bin, bout
  Multiplexer #(.width(8)) multiplexer_2 (
    .in0(register_2_q), .in1(ram_2_dout), .out(multiplexer_2_out), .sel(ALU_Inp_Select));
  Multiplexer #(.select(2), .width(8)) multiplexer_3 (
    .in0(ram_1_dout), .in1(out_16), .in2(out_17), .out(out_15), .sel(in_4));  // open: in3
  Adder adder_3 (.a(multiplexer_2_out), .b(8'h1), .out(adder_3_out));  // open: cin, cout
  Subtractor subtractor_3 (.a(multiplexer_2_out), .b(8'h1), .out(subtractor_3_out));  // open: bin, bout
  Demultiplexer #(.width(8)) demultiplexer_1 (
    .out0(demultiplexer_1_out0), .out1(demultiplexer_1_out1), .in(out_22), .sel(ALU_Inp_Select));
  Multiplexer #(.select(2), .width(8)) multiplexer_4 (
    .in0(multiplexer_2_out), .in1(adder_3_out), .in2(subtractor_3_out), .out(out_22), .sel(ALU_Oup_Select));  // open: in3

  // Notes on the sheet:
  //   Output of "selector OUT"
  //   contents of rom_1 (hex, n*v repeats v):
  //   0 1 2 3 4 5 6 7 8 9 a b c d e f 10
  //   selector IN
  //   Output of "selector OUT"
  //   Output of "selector OUT"
  //   selector IN
  //   selector IN
endmodule
