// Logisim project BFlogic_3.circ as structural Verilog: 3 circuits, main circuit main
module main (
  input  [7:0] in_1,
  input  in_2,
  input  [7:0] in_3,
  input  in_4,
  input  in_5,
  input  in_6,
  output [7:0] out_7,
  output out_8,
  output [7:0] out_9,
  output out_10,
  output out_11,
  output [7:0] SA,
  output [7:0] out_13,
  output out_14,
  output [1:0] out_15,
  output out_16,
  output [7:0] out_17,
  output out_18,
  output out_19,
  output out_20,
  output out_21,
  output [1:0] out_22,
  output out_23,
  output out_24,
  output out_25,
  output out_26,
  output out_27
);

  wire and_4_out, and_9_out, and_11_out, clock_1_out, comparator_2_eq, Flag_q, nand_1_out, nor_1_out,
       nor_2_out, nor_3_out, not_1_out, not_2_out, not_3_out, not_4_out, not_5_out, or_2_out;
  wire [4:0] rom_1_data;
  wire [7:0] adder_1_out, adder_2_out, counter_1_q, InputRegister_q, multiplexer_1_out, multiplexer_3_out,
       Nest_q, ram_1_dout, Stack_q, subtractor_1_out;

  RAM #(.asyncread("true")) ram_1 (
    .addr(out_17), .we(out_20), .oe(1'b1), .clk(clock_1_out), .din(counter_1_q), .dout(ram_1_dout));
  Clock clock_1 (.out(clock_1_out));
  Register Address (.D(out_7), .en(out_8), .clk(clock_1_out), .Q(out_9), .clr(in_2));
  Register InputRegister (.D(in_3), .en(in_4), .clk(clock_1_out), .Q(InputRegister_q), .clr(in_2));
  RAM #(.asyncread("true")) ram_2 (
    .addr(out_9), .we(out_11), .oe(1'b1), .clk(clock_1_out), .din(multiplexer_1_out), .dout(SA));
  Multiplexer #(.width(8)) multiplexer_1 (.in0(out_7), .in1(InputRegister_q), .out(multiplexer_1_out), .sel(out_14));
  Multiplexer #(.width(8)) multiplexer_2 (.in0(adder_2_out), .in1(Stack_q), .out(out_17), .sel(out_16));
  Adder adder_1 (.a(ram_1_dout), .b(8'h1), .out(adder_1_out));  // open: cin, cout
  Counter counter_1 (
    .clr(in_2), .load(out_25), .up(1'b1), .clk(clock_1_out), .D(adder_1_out), .Q(counter_1_q));  // open: count, carry
  Register Stack (.D(multiplexer_3_out), .en(out_21), .clk(clock_1_out), .Q(Stack_q), .clr(in_2));
  Register Nest (.D(Stack_q), .en(out_24), .clk(clock_1_out), .Q(Nest_q), .clr(in_2));
  and and_1 (out_11, not_2_out, and_4_out);
  and and_2 (out_8, nor_1_out, not_2_out);
  and and_3 (out_25, out_21, out_16, out_18);
  and and_4 (and_4_out, nand_1_out, out_15[0]);
  and and_5 (out_24, out_20, nor_2_out);
  Multiplexer #(.select(2), .width(8)) multiplexer_3 (
    .in1(adder_2_out), .in2(subtractor_1_out), .in3(Stack_q), .out(multiplexer_3_out),
    .sel({out_16, out_22[0]}));  // open: in0
  or or_1 (out_22[0], not_1_out, out_18);
  nand nand_1 (nand_1_out, out_14, out_16);
  nor nor_1 (nor_1_out, out_14, out_15[0]);
  and and_6 (out_20, out_21, not_4_out);
  and and_7 (out_26, out_21, or_2_out);
  Multiplexer #(.select(2), .width(8)) multiplexer_4 (
    .in0(out_9), .in1(SA), .in2(Stack_q), .out(out_13), .sel({out_14, out_15[0]}));  // open: in3
  ROM rom_1 (.addr(counter_1_q), .data({out_14, out_15[0], out_16, rom_1_data}));
  and and_8 (out_10, and_9_out, not_2_out);
  or or_2 (or_2_out, nor_3_out, and_11_out);
  Comparator #(.mode("unsigned"), .width(1)) comparator_1 (.a(in_5), .b(in_6), .eq(out_27));  // open: gt, lt
  Adder adder_2 (.a(out_13), .b(8'h1), .out(adder_2_out));  // open: cin, cout
  Subtractor subtractor_1 (.a(out_13), .b(8'h1), .out(subtractor_1_out));  // open: bin, bout
  not not_1 (not_1_out, out_16);
  and and_9 (and_9_out, out_14, out_15[0], out_16);
  and and_10 (out_21, out_14, not_3_out);
  nor nor_2 (nor_2_out, Flag_q, out_18);
  nor nor_3 (nor_3_out, out_16, Flag_q, out_18);
  and and_11 (and_11_out, out_16, Flag_q, out_23);
  Multiplexer #(.width(8)) multiplexer_5 (.in0(adder_2_out), .in1(subtractor_1_out), .out(out_7), .sel(out_16));
  Comparator #(.mode("unsigned")) comparator_2 (.a(SA), .b({8{1'b0}}), .eq(comparator_2_eq));  // open: gt, lt
  Comparator #(.mode("unsigned")) comparator_3 (.a(subtractor_1_out), .b(Nest_q), .eq(out_23));  // open: gt, lt
  not not_2 (not_2_out, Flag_q);
  not not_3 (not_3_out, out_15[0]);
  not not_4 (not_4_out, out_16);
  Register OutputRegister (.D(SA), .en(out_10), .clk(clock_1_out), .clr(in_2));  // open: Q
  Register #(.width(1)) Flag (.D(not_5_out), .en(out_26), .clk(clock_1_out), .Q(Flag_q), .clr(in_2));
  not not_5 (not_5_out, Flag_q);
  not not_6 (out_18, comparator_2_eq);
  TTY tty_1 (.data(SA[6:0]), .clk(clock_1_out), .we(out_10), .clr(in_2));

  assign out_15[1] = out_14;
  assign out_19 = out_16;
  assign out_22[1] = out_16;

  // Notes on the sheet:
  //   SD
  //   C
  //   St
  //   A
  //   V
  //   SD
  //   SE
  //   Np
  //   Sp
  //   F
  //   SB
  //   SB
  //   SA
  //   contents of rom_1 (hex, n*v repeats v):
  //   9*40 80 60 0 8*40 0 11*40 0 5*40 20 20 20 a0 0 e0 0 40 40 e0 7*40 e0 e0 40 40 40 e0 0 60 e0 12*60 e0
  //   20 8*40 e0 8*60 e0 40 40 40 e0 6*60 e0 8*60 e0 0 40 e0
  //   OUT
  //   SC
  //   SC
  //   I2
  //   I1
  //   I0
  //   F
  //   C1
  //   C0
endmodule

module test (
  input  D1,
  input  D0,
  output F,
  output out_4
);

  and and_1 (out_4, D1, D0);
  xor xor_1 (F, D1, D0);
endmodule

module dec (
  input  I2,
  input  I1,
  input  I0,
  input  F,
  input  C1,
  input  C0,
  input  [5:0] C0_2,
  output [15:0] out_8,
  output RA,
  output RSP,
  output RNP,
  output RF,
  output Val,
  output RKS,
  output CI,
  output O,
  output SA1,
  output SA0,
  output SB1,
  output SB0,
  output SC,
  output SD,
  output SE
);

  wire and_3_out, and_10_out, and_11_out, nand_1_out, nor_1_out, nor_2_out, nor_3_out, not_1_out, not_2_out,
       not_3_out, not_4_out, or_1_out;

  and and_1 (out_8[11], not_2_out, and_3_out);
  and and_2 (out_8[15], nor_1_out, not_2_out);
  and and_3 (and_3_out, nand_1_out, I1);
  and and_4 (out_8[13], out_8[10], nor_2_out);
  and and_5 (CI, out_8[14], I0, C1);
  nand nand_1 (nand_1_out, I2, I0);
  nor nor_1 (nor_1_out, I2, I1);
  and and_6 (out_8[10], out_8[14], not_4_out);
  and and_7 (out_8[12], out_8[14], or_1_out);
  nand nand_2 (out_8[4], I0, not_1_out);
  not not_1 (not_1_out, C1);
  and and_8 (O, and_10_out, not_2_out);
  and and_9 (out_8[14], I2, not_3_out);
  nor nor_2 (nor_2_out, F, C1);
  or or_1 (or_1_out, nor_3_out, and_11_out);
  and and_10 (and_10_out, I2, I1, I0);
  not not_2 (not_2_out, F);
  not not_3 (not_3_out, I1);
  not not_4 (not_4_out, I0);
  nor nor_3 (nor_3_out, I0, F, C1);
  and and_11 (and_11_out, I0, F, C0);

  assign {out_8[9:5], out_8[3:0]} = {CI, O, I2, I1, {2{I0}}, I2, I0, 1'b0};
  assign RA = out_8[15];
  assign RF = out_8[12];
  assign RKS = out_8[10];
  assign RNP = out_8[13];
  assign RSP = out_8[14];
  assign SA0 = I1;
  assign SA1 = I2;
  assign SB0 = out_8[4];
  assign SB1 = I0;
  assign SC = I0;
  assign SD = I2;
  assign SE = I0;
  assign Val = out_8[11];

  // Notes on the sheet:
  //   SC
  //   SA0
  //   SA1
  //   SB0
  //   SB1
  //   OUT
  //   Val
  //   Adr
  //   Sp
  //   Np
  //   St
  //   C
  //   Sd
  //   F
  //   I2
  //   I0
  //   I1
  //   C1
  //   F
endmodule
